# Fritzing sketch HarleenSaini_parkingEazeV1 (saved by Fritzing 0.9.3b)
circuit board: 8.74528cm x 5.85404cm
breadboards: 1

parts:
  EK1254_IR = fc-51 [package=THT]
  Harleen_Saini = Raspberry Pi B+

nets:
  N1: EK1254_IR.pin1, Harleen_Saini.GPIO4
  N2: EK1254_IR.pin2, Harleen_Saini.GND
  3V3: EK1254_IR.pin3, Harleen_Saini.3v3, Harleen_Saini.3V3

// code stored in the sketch: Untitled2.ino

int LED = 13; // Use the onboard Uno LED
int isObstaclePin = 4;  // This is our input pin
int isObstacle = HIGH;  // HIGH MEANS NO OBSTACLE

void setup() {
  pinMode(LED, OUTPUT);
  pinMode(isObstaclePin, INPUT);
  Serial.begin(9600);
  
}

void loop() {
  isObstacle = digitalRead(isObstaclePin);
  if (isObstacle == LOW)
  {
    Serial.println("OBSTACLE!!, OBSTACLE!!");
    digitalWrite(LED, HIGH);
  }
  else
  {
    Serial.println("clear");
    digitalWrite(LED, LOW);
  }
  delay(200);
}
