# Fritzing sketch HarleenSaini_parkingEazeV1_WithouRPi (saved by Fritzing 0.9.3b)
circuit board: 1.83151cm x 3.12036cm
breadboards: 1

parts:
  EK1254 = molex pin header, 3 pins [form=molex]
  part = double row male pin header, 8 pins [form="♂ (male)"]

nets:
  N1: EK1254.pin1, part.pin4
  N2: EK1254.pin2, part.pin7
  N3: EK1254.pin3, part.pin1

notes:
  Harleen Kaur Saini
  3v3
  GND
  OUT
  GPIO
  VCC
